# Fritzing sketch ebike_led_driver (saved by Fritzing 0.9.2b)
stripboards: 2

parts:
  Q5 = NPN-Transistor [package="TO92 [THT]"]
  ALIM = screw terminal, 2 pins
  R3 = Resistor [tolerance=±5% resistance=10k package=THT]
  R3_2 = Resistor [tolerance=±5% resistance=560m package=THT]
  Q4 = Basic FET N-Channel [package="DPak [SMD]"]
  LED1 = LED - 3mm [color="Red (633nm)" package="3 mm [THT]"]
  Q15 = Basic FET N-Channel [package="DPak [SMD]"]
  Q16 = NPN-Transistor [package="TO92 [THT]"]
  R4 = Resistor [tolerance=±5% resistance=10k package=THT]
  Commut_AV = screw terminal, 2 pins
  S5 = Round Pushbutton
  Q17 = Basic FET N-Channel [package="DPak [SMD]"]
  Q18 = NPN-Transistor [package="TO92 [THT]"]
  Commut_AR = screw terminal, 2 pins
  S6 = Round Pushbutton
  sortie_led_AR = screw terminal, 2 pins
  U1 = attiny85 [package=dip]
  ALIM1 = screw terminal, 2 pins
  Fuse1 = Fuse with Handler [part_number=Htc-15m]
  R30 = Resistor [tolerance=±5% resistance=10k package=THT]
  R31 = Resistor [tolerance=±1% resistance=560m package=THT]
  R32 = Resistor [tolerance=±1% resistance=560m package=THT]
  sortie_led_AV1 = screw terminal, 2 pins
  D3 = Rectifier Diode [part_number=1N4001 package="300 mil [THT]"]
  D5 = Rectifier Diode [part_number=1N4001 package="300 mil [THT]"]
  C3 = Ceramic Capacitor [capacitance=100nF package="100 mil [THT, multilayer]"]

nets:
  N1: Q5.E, ALIM.pin2, R3_2.Pin_1
  N2: Q5.B, R3_2.Pin_0, Q4.source
  N3: Q5.C, R3.Pin_0, Q4.Gate
  N4: ALIM.pin1, R3.Pin_1, LED1.anode
  N5: Q4.drain, LED1.cathode
  N6: Q15.Gate, Q16.C, R4.Pin_1
  N7: Q15.drain, sortie_led_AV1.pin2
  N8: Q15.source, Q16.B, R31.Pin_0
  N9: Q16.E, Commut_AV.pin2, S5.leg1, Q18.E, Commut_AR.pin1, S6.leg0, U1.Pin_4, ALIM1.pin2, R31.Pin_1, R32.Pin_0, C3.0
  N10: R4.Pin_0, U1.Pin_6
  N11: Commut_AV.pin1, S5.leg0, U1.Pin_2
  N12: Q17.Gate, Q18.C, R30.Pin_1
  N13: Q17.drain, sortie_led_AR.pin2
  N14: Q17.source, Q18.B, R32.Pin_1
  N15: Commut_AR.pin2, S6.leg1, U1.Pin_3
  N16: sortie_led_AR.pin1, Fuse1.Connector1, sortie_led_AV1.pin1, D3.anode
  N17: U1.Pin_5, R30.Pin_0
  N18: U1.Pin_8, D5.cathode, C3.1
  N19: ALIM1.pin1, Fuse1.Connector2
  N20: D3.cathode, D5.anode

notes:
  Led front -
  Led front +
  Led AV
  commutateur ON/OFF
  Led AR
  toujours alimentée
  commutateur / selecteur de puissance
  Led rear +
  Led rear -
  power GND
  power +6V
  boite
  83 x 108 x 50
